# Fritzing sketch AEG mignon schema (saved by Fritzing 0.9.4)
breadboards: 1

parts:
  Componente1 = Arduino Nano (Rev3.0)
  R1 = Slide Potentiometer [maximum_resistance=100kΩ]
  R2 = Slide Potentiometer [maximum_resistance=100kΩ]

nets:
  N1: Componente1.GND, R1.leg2, R2.leg2
  N2: Componente1.A4, R1.wiper
  N3: Componente1.A3, R2.wiper
  N4: Componente1.3V3, R1.leg1, R2.leg1
